# Fritzing sketch design (saved by Fritzing 0.9.5d)
circuit board: 8.46667cm x 5.64444cm
perfboards: 2

parts:
  U1 = 7-SEGMENT-4DIGIT-YOUNGSUN [package=7-segment-4digit-youngsun-longpads]
  R1 = Resistor [tolerance=±5% resistance=220 package=THT]
  R2 = Resistor [tolerance=±5% resistance=220 package=THT]
  R3 = Resistor [tolerance=±5% resistance=220 package=THT]
  R4 = Resistor [tolerance=±5% resistance=220 package=THT]
  R5 = Resistor [tolerance=±5% resistance=220 package=THT]
  R6 = Resistor [tolerance=±5% resistance=220 package=THT]
  R7 = Resistor [tolerance=±5% resistance=220 package=THT]
  Part1 = Arduino Nano (Rev3.0)

nets:
  N1: U1.DIG2, R1.Pin_1
  N2: U1.D, R2.Pin_1
  N3: U1.E, R3.Pin_1
  N4: U1.DIG3, R4.Pin_1
  N5: U1.DP, Part1.D9
  N6: U1.APOS-A, R7.Pin_0
  N7: U1.F, Part1.D10
  N8: U1.COL-C, Part1.D11/MOSI
  N9: U1.C, R6.Pin_0
  N10: U1.A, R5.Pin_0
  N11: U1.G, Part1.D12/MISO
  N12: R1.Pin_0, Part1.D6
  N13: R2.Pin_0, Part1.D5
  N14: R3.Pin_0, Part1.D4
  N15: R4.Pin_0, Part1.D8
  N16: R5.Pin_1, Part1.D2
  N17: R6.Pin_1, Part1.D7
  N18: R7.Pin_1, Part1.D3
