# Fritzing sketch design (saved by Fritzing 0.9.5d)
perfboards: 2

parts:
  Part1 = Arduino Nano (Rev3.0)
  LED1 = LED - 5mm [color="Red (633nm)" package="5 mm [THT]"]  # not connected
  LED2 = LED - 5mm [color="Red (633nm)" package="5 mm [THT]"]
  LED3 = LED - 5mm [color="Red (633nm)" package="5 mm [THT]"]  # not connected
  LED4 = LED - 5mm [color="Yellow (595nm)" package="5 mm [THT]"]  # not connected
  LED5 = LED - 5mm [color="Yellow (595nm)" package="5 mm [THT]"]  # not connected
  LED6 = LED - 5mm [color="Yellow (595nm)" package="5 mm [THT]"]  # not connected
  LED7 = LED - 5mm [color="Green (560nm)" package="5 mm [THT]"]  # not connected
  LED8 = LED - 5mm [color="Green (560nm)" package="5 mm [THT]"]
  LED9 = LED - 5mm [color="Green (560nm)" package="5 mm [THT]"]
  R1 = Resistor [tolerance=±5% resistance=220 package=THT]
  R2 = Resistor [tolerance=±5% resistance=1k package=THT]
  R3 = Resistor [tolerance=±5% resistance=220 package=THT]
  R4 = Resistor [tolerance=±5% resistance=220 package=THT]
  R5 = Resistor [tolerance=±5% resistance=1k package=THT]
  R6 = Resistor [tolerance=±5% resistance=1k package=THT]
  R7 = Resistor [tolerance=±5% resistance=10k package=THT]
  R8 = Resistor [tolerance=±5% resistance=10k package=THT]
  R9 = Resistor [tolerance=±5% resistance=10k package=THT]
  Part2 = Arduino Nano (Rev3.0)
  R10 = Resistor [tolerance=±5% resistance=220 package=THT]
  SG1 = Buzzer 12mm [package=buzzer-12mm-ns]
  S1 = Pushbutton [package="[THT]"]
  S2 = Pushbutton [package="[THT]"]
  R11 = Resistor [tolerance=±5% resistance=100k package=THT]
  R12 = Resistor [tolerance=±5% resistance=100k package=THT]

nets:
  N1: Part1.GND, R11.Pin_0, R12.Pin_0
  N2: Part1.D2, R2.Pin_0
  N3: Part1.D3, R5.Pin_0
  N4: Part1.D4, R6.Pin_0
  N5: Part1.D5, R1.Pin_0
  N6: Part1.D6, R3.Pin_0
  N7: Part1.D7, R4.Pin_0
  N8: Part1.D8, R7.Pin_0
  N9: Part1.D9, R8.Pin_0
  N10: Part1.D10, LED8.anode
  N11: Part1.D12/MISO, R9.Pin_0
  N12: Part1.A7, S2.Pin_1, S2.Pin_2
  N13: Part1.A6, S1.Pin_1, S1.Pin_2
  N14: LED2.anode, LED9.anode
  N15: Part2.GND, SG1.2
  N16: Part2.D11/MOSI, R10.Pin_0
  N17: R10.Pin_1, SG1.1
  N18: S1.Pin_3, S1.Pin_4
  N19: S2.Pin_3, S2.Pin_4
